// Logisim project braile.circ as structural Verilog: 2 circuits, main circuit main
module main (
  input  A,
  input  B,
  input  C,
  input  D,
  output W,
  output X,
  output Z,
  output Y
);

  wire and_1_out, and_2_out, and_3_out, and_4_out, and_5_out, and_6_out, and_7_out, or_1_out, xor_1_out;

  xor xor_1 (xor_1_out, D, A);
  and and_1 (and_1_out, A, D);
  or or_1 (or_1_out, B, D);
  and and_2 (and_2_out, ~D, ~C, ~A);  // AND_Gate
  and and_3 (and_3_out, B, D);
  and and_4 (and_4_out, ~D, ~B);  // AND_Gate
  and and_5 (and_5_out, ~B, ~D);  // AND_Gate
  and and_6 (and_6_out, B, C);
  or or_2 (W, xor_1_out, C, B);
  and and_7 (and_7_out, or_1_out, C);
  or or_3 (Y, and_3_out, and_4_out);
  or or_4 (Z, and_5_out, and_6_out, A);
  or or_5 (X, and_1_out, and_7_out, and_2_out);
endmodule

module DDD (
);

  main main_1 ();  // open: X, Z, Y, A, B, C, D, W
endmodule
